# Fritzing sketch project-WiE-October2019 (saved by Fritzing 0.9.3b)
breadboards: 1

parts:
  Εξάρτημα1 = Arduino Uno (Rev3) - ICSP
  R1 = Resistor [tolerance=±5% resistance=220 package="0603 [SMD]"]
  LED1 = smd LED [color="Red (633nm)" package="1206 [SMD]"]
  R2 = PHOTOCELL [package=photocell-kit]
  R3 = Resistor [tolerance=±5% resistance=1k package="0805 [SMD]"]

nets:
  N1: Εξάρτημα1.A0, R2.P$2, R3.Pin_0
  N2: Εξάρτημα1.D13/SCK, LED1.cathode
  N3: Εξάρτημα1.5V, R2.P$1
  N4: Εξάρτημα1.GND, R1.Pin_1, R3.Pin_1
  N5: R1.Pin_0, LED1.anode

notes:
  220Ω
  1kΩ
